# Fritzing sketch led controller 2 (saved by Fritzing 0.9.3b)
breadboards: 1

parts:
  S4 = Pushbutton [package="[SMD]"]
  LED1 = LED - 5mm [color="Red (633nm)" package="5 mm [THT]"]
  R2 = Resistor [tolerance=±5% resistance=220 package=THT]
  Raspberry_Pi_1 = Raspberry Pi 3 [part_number=RPI-3-V1.2]  # not connected
  Part3 = Adafruit T-Cobbler Plus [part_number="Adafruit #1989 and #2028"]
  LED3 = RGB LED (com. cathode, rgb) [package="5 mm [THT]"]
  R8 = Resistor [tolerance=±5% resistance=220 package=THT]
  R9 = Resistor [tolerance=±5% resistance=220 package=THT]
  R10 = Resistor [tolerance=±5% resistance=220 package=THT]
  S5 = Pushbutton [package="[SMD]"]
  LED4 = smd LED [color="Blue (470nm)" package="0603 [SMD]"]
  R11 = Resistor [tolerance=±5% resistance=220 package=THT]

nets:
  N1: S4.Pin_1, S4.Pin_2, R2.Pin_1
  N2: S4.Pin_3, S4.Pin_4, Part3.GND, LED3.common_cathode, R11.Pin_1
  N3: LED1.cathode, R2.Pin_0
  N4: LED1.anode, Part3.+5V, S5.Pin_3, S5.Pin_4, LED4.anode
  N5: LED3.red_anode, R8.Pin_0
  N6: LED3.green_anode, R9.Pin_0
  N7: LED3.blue_anode, R10.Pin_0
  N8: R8.Pin_1, R9.Pin_1, R10.Pin_1, S5.Pin_1, S5.Pin_2
  N9: LED4.cathode, R11.Pin_0

custom parts:
  Adafruit T-Cobbler Plus: The Raspberry Pi has landed on the Maker World like a 40-GPIO pinned, quad-USB ported, credit card sized bomb of DIY joy. And while you can use most of our great Model B accessories by hooking up our downgrade cable, its probably a good time to upgrade your set up and accessorize using all of the 40 pins. That's why we now carry the Assembled Adafruit Pi T-Cobbler Plus - Breakout + Cable for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
