# Fritzing sketch color-controller (saved by Fritzing 0.9.3b)
breadboards: 1

parts:
  Raspberry_Pi_1 = Raspberry Pi 3 [part_number=RPI-3-V1.2]  # not connected
  Part3 = Adafruit T-Cobbler Plus [part_number="Adafruit #1989 and #2028"]
  LED3 = RGB LED (com. cathode, rgb) [package="5 mm [THT]"]
  R8 = Resistor [tolerance=±5% resistance=220 package=THT]
  R9 = Resistor [tolerance=±5% resistance=220 package=THT]
  R10 = Resistor [tolerance=±5% resistance=220 package=THT]
  LED4 = smd LED [color="Yellow (592nm)" package="0603 [SMD]"]
  R11 = Resistor [tolerance=±5% resistance=220 package=THT]

nets:
  N1: Part3.GND, LED3.common_cathode, R11.Pin_1
  N2: Part3.GPIO13, R10.Pin_1
  N3: Part3.GPIO19, R9.Pin_1
  N4: Part3.GPIO26, R8.Pin_1
  N5: Part3.GPIO21, LED4.anode
  N6: LED3.red_anode, R8.Pin_0
  N7: LED3.green_anode, R9.Pin_0
  N8: LED3.blue_anode, R10.Pin_0
  N9: LED4.cathode, R11.Pin_0

notes:
  These power connections are already made by Canakit Cobblers

custom parts:
  Adafruit T-Cobbler Plus: The Raspberry Pi has landed on the Maker World like a 40-GPIO pinned, quad-USB ported, credit card sized bomb of DIY joy. And while you can use most of our great Model B accessories by hooking up our downgrade cable, its probably a good time to upgrade your set up and accessorize using all of the 40 pins. That's why we now carry the Assembled Adafruit Pi T-Cobbler Plus - Breakout + Cable for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
