# Fritzing sketch 3-leds (saved by Fritzing 0.9.3b)
breadboards: 1

parts:
  Raspberry_Pi_1 = Raspberry Pi 3 [part_number=RPI-3-V1.2]  # not connected
  Part3 = Adafruit T-Cobbler Plus [part_number="Adafruit #1989 and #2028"]
  LED4 = smd LED [color="Yellow (592nm)" package="0603 [SMD]"]
  R11 = Resistor [tolerance=±5% resistance=220 package=THT]
  LED5 = smd LED [color="Green (555nm)" package="0603 [SMD]"]
  R12 = Resistor [tolerance=±5% resistance=220 package=THT]
  LED6 = smd LED [color="Blue (470nm)" package="0603 [SMD]"]
  R13 = Resistor [tolerance=±5% resistance=220 package=THT]

nets:
  N1: Part3.GND, R11.Pin_1, R12.Pin_1, R13.Pin_1
  N2: Part3.GPIO16, LED6.anode
  N3: Part3.GPIO20, LED5.anode
  N4: Part3.GPIO21, LED4.anode
  N5: LED4.cathode, R11.Pin_0
  N6: LED5.cathode, R12.Pin_0
  N7: LED6.cathode, R13.Pin_0

notes:
  These power connections are already made by Canakit Cobblers

custom parts:
  Adafruit T-Cobbler Plus: The Raspberry Pi has landed on the Maker World like a 40-GPIO pinned, quad-USB ported, credit card sized bomb of DIY joy. And while you can use most of our great Model B accessories by hooking up our downgrade cable, its probably a good time to upgrade your set up and accessorize using all of the 40 pins. That's why we now carry the Assembled Adafruit Pi T-Cobbler Plus - Breakout + Cable for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
