# Fritzing sketch neopixel-bb (saved by Fritzing 0.9.3b)
breadboards: 1

parts:
  Raspberry_Pi_1 = Raspberry Pi 3 [part_number=RPI-3-V1.2]  # not connected
  Part3 = Adafruit T-Cobbler Plus [part_number="Adafruit #1989 and #2028"]
  NEOPIXEL1 = Neopixel Strip -- Black (30/m) [part_number=1376]

nets:
  GND: Part3.GND, NEOPIXEL1.GND
  +5V: Part3.+5V, NEOPIXEL1.+5V
  N1: Part3.GPIO18, NEOPIXEL1.Dout

notes:
  These power connections are already made by Canakit Cobblers

custom parts:
  Adafruit T-Cobbler Plus: The Raspberry Pi has landed on the Maker World like a 40-GPIO pinned, quad-USB ported, credit card sized bomb of DIY joy. And while you can use most of our great Model B accessories by hooking up our downgrade cable, its probably a good time to upgrade your set up and accessorize using all of the 40 pins. That's why we now carry the Assembled Adafruit Pi T-Cobbler Plus - Breakout + Cable for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
  Neopixel Strip -- Black (30/m): These NeoPixel strips have 30 digitally-addressable pixel LEDs per meter and are very affordable and are only 12.5 mm wide, 10 mm if you remove the strip from the casing.
